# Fritzing sketch base board v3 (saved by Fritzing 0.9.3b)
circuit board: 5.07504cm x 4.75559cm
stripboards: 1

parts:
  Part1 = Arduino Nano (Rev3.0)
  ThO = female pin header, 1 pin [form="♀ (female)"]
  RL = IC, DIP package, 16 pins [chip_label=IC]
  US = female pin header, 4 pins [form="♀ (female)"]
  SRV = female pin header, 3 pins [form="♀ (female)"]
  RTh = female pin header, 1 pin [form="♀ (female)"]
  BT = female pin header, 5 pins [form="♀ (female)"]
  RX_IN = female pin header, 1 pin [form="♀ (female)"]
  PWR = female pin header, 2 pins [form="♀ (female)"]
  LED1 = LED - 3mm [color="Red (633nm)" package="3 mm [THT]"]
  R1 = Resistor [tolerance=±5% resistance=470 package=THT]
  AUX1 = female pin header, 1 pin [form="♀ (female)"]

nets:
  N1: Part1.D1/TX, BT.pin4
  N2: Part1.D0/RX, BT.pin3
  N3: Part1.GND, RL.pin1, US.pin4, SRV.pin3, BT.pin2, PWR.pin2, R1.Pin_1
  N4: Part1.D3, SRV.pin1
  N5: Part1.D4, RX_IN.pin1
  N6: Part1.D6, AUX1.pin1
  N7: Part1.D7, US.pin3
  N8: Part1.D8, US.pin2
  N9: Part1.D11/MOSI, RL.pin16
  N10: Part1.D12/MISO, RL.pin9
  N11: Part1.VIN, US.pin1, SRV.pin2, BT.pin1, PWR.pin1
  N12: ThO.pin1, RL.pin13
  N13: RL.pin11, RTh.pin1
  N14: BT.pin5, LED1.anode
  N15: LED1.cathode, R1.Pin_0
